// Logisim project ex5.circ as structural Verilog: 5 circuits, main circuit rotr
module rotr (
  input  [15:0] A,
  input  [3:0] B,
  output [15:0] Out1
);

  wire [15:0] x1, x2, x3, x4, x5, x6, x7, x8, x9, x10, x11, x12, x13, x14, x15;

  rot8 rot8_1 (.in_1(A), .out_2(x8));
  rot4 rot4_1 (.in_1(A), .out_2(x4));
  rot4 rot4_2 (.in_1(x8), .out_2(x12));
  rot2 rot2_1 (.in_1(x8), .out_2(x10));
  rot1 rot1_1 (.in_1(x8), .out_2(x9));
  rot2 rot2_2 (.in_1(x4), .out_2(x6));
  rot1 rot1_2 (.in_1(A), .out_2(x1));
  rot1 rot1_3 (.in_1(x1), .out_2(x2));
  rot2 rot2_3 (.in_1(x12), .out_2(x14));
  rot1 rot1_4 (.in_1(x14), .out_2(x15));
  rot1 rot1_5 (.in_1(x12), .out_2(x13));
  rot1 rot1_6 (.in_1(x10), .out_2(x11));
  rot1 rot1_7 (.in_1(x6), .out_2(x7));
  rot1 rot1_8 (.in_1(x4), .out_2(x5));
  rot1 rot1_9 (.in_1(x2), .out_2(x3));
  Multiplexer #(.enable("false"), .select(4), .width(16)) multiplexer_1 (
    .in0(A), .in1(x1), .in2(x2), .in3(x3), .in4(x4), .in5(x5), .in6(x6), .in7(x7), .in8(x8), .in9(x9),
    .in10(x10), .in11(x11), .in12(x12), .in13(x13), .in14(x14), .in15(x15), .out(Out1), .sel(B));

  // Other names for the same wires on the sheet: x0[15:0] = A
endmodule

module rot8 (
  input  [15:0] in_1,
  output [15:0] out_2
);

  wire [15:0] rot4_1_out_2;

  rot4 rot4_1 (.in_1(in_1), .out_2(rot4_1_out_2));
  rot4 rot4_2 (.in_1(rot4_1_out_2), .out_2(out_2));

  // Notes on the sheet:
  //   PUT CIRCUITRY HERE
endmodule

module rot4 (
  input  [15:0] in_1,
  output [15:0] out_2
);

  wire [15:0] rot2_1_out_2;

  rot2 rot2_1 (.in_1(in_1), .out_2(rot2_1_out_2));
  rot2 rot2_2 (.in_1(rot2_1_out_2), .out_2(out_2));

  // Notes on the sheet:
  //   PUT CIRCUITRY HERE
endmodule

module rot2 (
  input  [15:0] in_1,
  output [15:0] out_2
);

  wire [15:0] rot1_1_out_2;

  rot1 rot1_1 (.in_1(in_1), .out_2(rot1_1_out_2));
  rot1 rot1_2 (.in_1(rot1_1_out_2), .out_2(out_2));

  // Notes on the sheet:
  //   PUT CIRCUITRY HERE
endmodule

module rot1 (
  input  [15:0] in_1,
  output [15:0] out_2
);


  assign out_2 = {in_1[0], in_1[15:1]};

  // Notes on the sheet:
  //   PUT CIRCUITRY HERE
endmodule
