// Logisim project branch_comp.circ as structural Verilog: 1 circuit, main circuit branch_comp
module branch_comp (
  input  [31:0] rs1,
  input  [31:0] rs2,
  input  BrUn,
  output BrEq,
  output BrLt
);

  wire signedEq, singedLt, usignedEq, usingedLt;

  Comparator #(.width(32)) comparator_1 (.a(rs1), .b(rs2), .eq(signedEq), .lt(singedLt));  // open: gt
  Comparator #(.mode("unsigned"), .width(32)) comparator_2 (
    .a(rs1), .b(rs2), .eq(usignedEq), .lt(usingedLt));  // open: gt
  Multiplexer #(.enable("false")) multiplexer_1 (.in0(signedEq), .in1(usignedEq), .out(BrEq), .sel(BrUn));
  Multiplexer #(.enable("false")) multiplexer_2 (.in0(singedLt), .in1(usingedLt), .out(BrLt), .sel(BrUn));

  // Notes on the sheet:
  //   INPUTS to your circuit
  //   DON'T CHANGE THE LOCATIONS OF THE INPUTS AND OUTPUTS!
  //   OUTPUT from your circuit
endmodule
