// Logisim project control_logic.circ as structural Verilog: 1 circuit, main circuit control_logic
module control_logic (
  input  [31:0] inst,
  input  BrEq,
  input  BrLt,
  output PCSel,
  output RegWEn,
  output [2:0] ImmSel,
  output BrUn,
  output ASel,
  output BSel,
  output [3:0] ALUSel,
  output MemRW,
  output [1:0] WBSel,
  output CSRSel,
  output CSRWen
);

  wire and2, and_1_out, and_2_out, and_3_out, and_4_out, and_5_out, and_6_out, and_8_out, and_9_out, asel2,
       auipc, bsel_t, csr_imm, fun3_0, fun3_1, fun3_2, fun3_3, fun3_4, fun3_5, fun3_6, fun3_7, fun7_0,
       fun7_1, fun7_20, gt, I, I_Load, jarl, mul2, mulh2, mulhu2, NEq, or2, or_1_out, or_2_out, R, sll2,
       slt2, sra2, srl2, sub2, UJ, xor2;
  wire [2:0] helpSel;

  Comparator #(.width(7)) comparator_1 (.a(inst[6:0]), .b(7'b0110011), .eq(R));  // open: gt, lt
  Comparator #(.width(7)) comparator_2 (.a(inst[6:0]), .b(7'b0000011), .eq(I_Load));  // open: gt, lt
  Comparator #(.width(7)) comparator_3 (.a(inst[6:0]), .b(7'b0010011), .eq(I));  // open: gt, lt
  Comparator #(.width(7)) comparator_4 (.a(inst[6:0]), .b(7'b0100011), .eq(MemRW));  // open: gt, lt
  Comparator #(.width(7)) comparator_5 (.a(inst[6:0]), .b(7'b1100011), .eq(ASel));  // open: gt, lt
  Comparator #(.width(7)) comparator_6 (.a(inst[6:0]), .b(7'b0010111), .eq(auipc));  // open: gt, lt
  Comparator #(.width(7)) comparator_7 (.a(inst[6:0]), .b(7'b0110111), .eq(bsel_t));  // open: gt, lt
  Comparator #(.width(7)) comparator_8 (.a(inst[6:0]), .b(7'b1101111), .eq(UJ));  // open: gt, lt
  Comparator #(.width(7)) comparator_9 (.a(inst[6:0]), .b(7'b1100111), .eq(jarl));  // open: gt, lt
  Comparator #(.width(7)) comparator_10 (.a(inst[6:0]), .b(7'b1110011), .eq(CSRSel));  // open: gt, lt
  Demultiplexer #(.enable("false"), .select(3)) demultiplexer_1 (
    .out0(fun3_0), .out1(fun3_1), .out2(fun3_2), .out3(fun3_3), .out4(fun3_4), .out5(fun3_5), .out6(fun3_6),
    .out7(fun3_7), .in(1'b1), .sel(inst[14:12]));
  Comparator #(.mode("unsigned"), .width(7)) comparator_11 (
    .a(inst[31:25]), .b({7{1'b0}}), .eq(fun7_0));  // open: gt, lt
  Comparator #(.mode("unsigned"), .width(7)) comparator_12 (
    .a(inst[31:25]), .b(7'b0000001), .eq(fun7_1));  // open: gt, lt
  Comparator #(.mode("unsigned"), .width(7)) comparator_13 (
    .a(inst[31:25]), .b(7'b0100000), .eq(fun7_20));  // open: gt, lt
  not not_1 (NEq, BrEq);
  not not_2 (gt, BrLt);
  or or_1 (or_1_out, gt, BrEq);
  or or_2 (or_2_out, gt, BrEq);
  and and_1 (and_1_out, ASel, fun3_0, BrEq);
  and and_2 (and_2_out, ASel, fun3_1, NEq);
  and and_3 (and_3_out, ASel, fun3_4, BrLt, NEq);
  and and_4 (and_4_out, ASel, fun3_5, or_1_out);
  and and_5 (and_5_out, ASel, fun3_6, BrLt, NEq);
  and and_6 (and_6_out, ASel, fun3_7, or_2_out);
  or or_3 (PCSel, and_1_out, and_2_out, and_3_out, and_4_out, and_5_out, and_6_out);
  and and_7 (csr_imm, CSRSel, fun3_5);
  or or_4 (RegWEn, R, I_Load, I, auipc, bsel_t, UJ, jarl);
  or or_5 (helpSel[2], csr_imm, UJ);
  or or_6 (helpSel[1], ASel, auipc, bsel_t);
  or or_7 (helpSel[0], MemRW, auipc, csr_imm, bsel_t);
  Multiplexer #(.enable("false"), .select(3), .width(3)) multiplexer_1 (
    .in0(3'b000), .in1(3'b001), .in2(3'b010), .in3(3'b011), .in4(3'b100), .in5(3'b101), .out(ImmSel),
    .sel(helpSel));  // open: in6, in7
  and and_8 (and_8_out, ASel, fun3_6);
  and and_9 (and_9_out, ASel, fun3_7);
  or or_8 (BrUn, and_8_out, and_9_out);
  or or_9 (BSel, I, I_Load, jarl, csr_imm, MemRW, ASel, auipc, bsel_t, UJ, 1'b0);
  and mul (mul2, R, fun3_0, fun7_1);
  and mulhu (mulhu2, R, fun3_3, fun7_1);
  and mulh (mulh2, R, fun3_1, fun7_1);
  and sub (sub2, R, fun3_0, fun7_20);
  and my_asel (asel2, CSRSel, fun3_1);
  and u_srl2 (srl2, R, fun3_5, fun7_0);
  and u_sra2 (sra2, R, fun3_5, fun7_20);
  and u_sll2 (sll2, R, fun3_1, fun7_0);
  and u_slt2 (slt2, R, fun3_2, fun7_0);
  and and_10 (or2, R, fun3_6, fun7_0);
  and and_11 (xor2, R, fun3_4, fun7_0);
  and and_12 (and2, R, fun3_7, fun7_0);
  or or_10 (ALUSel[3], mul2, mulhu2, mulh2, sub2, 1'b0, bsel_t);
  or or_11 (ALUSel[2], srl2, sra2, sll2, slt2, bsel_t, sub2, mulh2);
  or or_12 (ALUSel[1], or2, xor2, sll2, slt2, mul2, mulhu2, mulh2);
  or or_13 (ALUSel[0], and2, xor2, sra2, slt2, mulhu2, bsel_t);
  or or_14 (WBSel[0], R, I, auipc, bsel_t);
  or or_15 (WBSel[1], UJ, jarl);

  assign CSRWen = CSRSel;

  // Other names for the same wires on the sheet: helpAlu_0 = ALUSel[0]; helpAlu_1 = ALUSel[1]; helpAlu_2 = ALUSel[2];
  //   helpAlu_3 = ALUSel[3]; I_csrw = CSRSel; opcode[6:0] = inst[6:0]; rd[4:0] = inst[11:7]; func3[2:0] = inst[14:12];
  //   rs1[4:0] = inst[19:15]; rs2[4:0] = inst[24:20]; fun7_or_Imm[6:0] = inst[31:25]; lui = bsel_t; S = MemRW;
  //   SB = ASel

  // Notes on the sheet:
  //   INPUTS to your circuit
  //   DON'T CHANGE THE LOCATIONS OF THE INPUTS AND OUTPUTS!
  //   OUTPUT from your circuit
endmodule
