// Logisim project cpu.circ as structural Verilog: 1 circuit, main circuit cpu
module cpu (
  input  clk,
  input  [31:0] INSTRUCTION,
  input  [31:0] READ_DATA,
  output [31:0] WRITE_ADDRESS,
  output [31:0] PROGRAM_COUNTER,
  output [31:0] ra,
  output [31:0] sp,
  output [31:0] t0,
  output [31:0] t1,
  output [31:0] t2,
  output [31:0] s0,
  output [31:0] s1,
  output [31:0] a0,
  output [31:0] tohost,
  output [3:0] WRITE_ENABLE,
  output [31:0] WRITE_DATA
);

  wire ASel, BrEq, BrLt, BrUn, BSel, \byte , CSRSel, CSRWen, hw, MemRW, PCSel, w_bit0, w_bit2, w_bit3, w_en;
  wire [1:0] WBSel;
  wire [2:0] fun3, ImmSel;
  wire [3:0] ALUSel;
  wire [4:0] rs2;
  wire [31:0] data1, IFEX, imm, multiplexer_1_out, multiplexer_2_out, nextIns, pc_plus_4;

  Adder #(.width(32)) adder_1 (.a(PROGRAM_COUNTER), .b(32'h4), .out(pc_plus_4));  // open: cin, cout
  Register #(.width(32)) PC (.D(nextIns), .clk(clk), .Q(PROGRAM_COUNTER));  // open: en, clr
  Multiplexer #(.enable("false"), .width(32)) multiplexer_1 (
    .in0(data1), .in1(PROGRAM_COUNTER), .out(multiplexer_1_out), .sel(ASel));
  Multiplexer #(.enable("false"), .width(32)) multiplexer_2 (
    .in0(WRITE_DATA), .in1(imm), .out(multiplexer_2_out), .sel(BSel));
  control_logic control_logic_1 (
    .CSRWen(CSRWen), .PCSel(PCSel), .RegWEn(w_en), .ImmSel(ImmSel), .BrUn(BrUn), .ASel(ASel), .BSel(BSel),
    .ALUSel(ALUSel), .MemRW(MemRW), .WBSel(WBSel), .CSRSel(CSRSel), .inst({IFEX[31:15], fun3, IFEX[11:0]}),
    .BrEq(BrEq), .BrLt(BrLt));
  imm_gen imm_gen_1 (.inst({IFEX[31:15], fun3, IFEX[11:0]}), .ImmSel(ImmSel), .imm(imm));
  alu alu_1 (.Result(WRITE_ADDRESS), .A(multiplexer_1_out), .B(multiplexer_2_out), .ALUSel(ALUSel));
  regfile regfile_1 (
    .rs1(IFEX[19:15]), .rs2(rs2), .rd(IFEX[11:7]), .RegWEn(w_en), .clk(clk), .ra(ra), .sp(sp), .t0(t0),
    .t1(t1), .t2(t2), .s0(s0), .s1(s1), .a0(a0), .Read_Data_1(data1), .Read_Data_2(WRITE_DATA));  // open: Write_Data
  csr csr_1 (.tohost(tohost));  // open: CSR_address, CSR_din, CSR_WE, clk
  branch_comp branch_comp_1 (.rs1(data1), .rs2(WRITE_DATA), .BrUn(BrUn), .BrEq(BrEq), .BrLt(BrLt));
  Register #(.width(32)) register_1 (.D(INSTRUCTION), .clk(clk), .Q({IFEX[31:15], fun3, IFEX[11:0]}));  // open: en, clr
  Multiplexer #(.enable("false"), .width(4)) multiplexer_3 (
    .in0(4'b0000), .in1({w_bit3, w_bit2, {2{w_bit0}}}), .out(WRITE_ENABLE), .sel(MemRW));
  Multiplexer #(.enable("false"), .select(2), .width(32)) multiplexer_4 (
    .in0(READ_DATA), .in1(WRITE_ADDRESS), .in2(pc_plus_4), .out(nextIns), .sel(WBSel));  // open: in3
  Comparator #(.mode("unsigned"), .width(3)) comparator_1 (.a(fun3), .b(3'b000), .eq(\byte ));  // open: gt, lt
  Comparator #(.mode("unsigned"), .width(3)) comparator_2 (.a(fun3), .b(3'b001), .eq(hw));  // open: gt, lt
  Comparator #(.mode("unsigned"), .width(3)) comparator_3 (.a(fun3), .b(3'b010), .eq(w_bit0));  // open: gt, lt
  or or_1 (w_bit3, \byte , hw, w_bit0);
  or or_2 (w_bit2, hw, w_bit0);

  // Other names for the same wires on the sheet: w_bit1 = w_bit0; word = w_bit0; AluOut[31:0] = WRITE_ADDRESS;
  //   data2[31:0] = WRITE_DATA; opcode[6:0] = IFEX[6:0]; rd[4:0] = IFEX[11:7]; IFEX[14:12] = fun3;
  //   rs1[4:0] = IFEX[19:15]

  // Notes on the sheet:
  //   Output to IMEM
  //   IMEM (do **NOT** move this)
  //   Inputs from IMEM
  //   It is OK to move the PC, RegFile, ALU, MEM, Branch Comp, Imm Gen, and Control Logic to wherever is most convenient for you when constructing your CPU, and to delete this text
  //   Inputs/Outputs for testing. Do **NOT** move these.
  //   Outputs To DMEM
  //   DMEM (do **NOT** move this)
  //   Inputs From DMEM
endmodule
