// Logisim project imm_gen.circ as structural Verilog: 1 circuit, main circuit imm_gen
module imm_gen (
  input  [31:0] inst,
  input  [2:0] ImmSel,
  output [31:0] imm
);

  wire [31:0] csr_imm, I, S, SB, UJ;

  assign I = {{20{inst[31]}}, inst[31:20]};  // Bit_Extender bit_extender_1
  assign S = {{20{inst[31]}}, {inst[31:25], inst[11:7]}};  // Bit_Extender bit_extender_2
  assign csr_imm = {{27{1'b0}}, inst[19:15]};  // Bit_Extender bit_extender_3
  assign SB = {{19{inst[31]}}, {inst[31], inst[7], inst[30:25], inst[11:8], 1'b0}};  // Bit_Extender bit_extender_4
  assign UJ = {{11{inst[31]}}, {inst[31], inst[19:12], inst[20], inst[30:21], 1'b0}};  // Bit_Extender bit_extender_5
  Multiplexer #(.enable("false"), .select(3), .width(32)) multiplexer_1 (
    .in0(I), .in1(S), .in2(SB), .in3({inst[31:12], {12{1'b0}}}), .in4(UJ), .in5(csr_imm), .out(imm),
    .sel(ImmSel));  // open: in6, in7

  // Other names for the same wires on the sheet: e_11[3:0] = inst[11:8]; se = inst[7]; tf_tt[9:0] = inst[30:21];
  //   U[31:12] = inst[31:12]; tf_t[5:0] = inst[30:25]; tw = inst[20]; tw_nt[7:0] = inst[19:12]; tf = inst[31];
  //   tf2 = inst[31]

  // Notes on the sheet:
  //   INPUTS to your circuit
  //   DON'T CHANGE THE LOCATIONS OF THE INPUTS AND OUTPUTS!
  //   OUTPUT from your circuit
endmodule
