// Logisim project regfile.circ as structural Verilog: 1 circuit, main circuit regfile
module regfile (
  input  [4:0] rs1,
  input  [4:0] rs2,
  input  [4:0] rd,
  input  [31:0] Write_Data,
  input  RegWEn,
  input  clk,
  output [31:0] ra,
  output [31:0] sp,
  output [31:0] t0,
  output [31:0] t1,
  output [31:0] t2,
  output [31:0] s0,
  output [31:0] s1,
  output [31:0] a0,
  output [31:0] Read_Data_1,
  output [31:0] Read_Data_2
);

  wire comparator_1_eq, comparator_2_eq, comparator_3_eq, comparator_4_eq, comparator_5_eq, comparator_6_eq,
       comparator_7_eq, comparator_8_eq, comparator_9_eq, comparator_10_eq, comparator_11_eq,
       comparator_12_eq, comparator_13_eq, comparator_14_eq, comparator_15_eq, comparator_16_eq,
       comparator_17_eq, comparator_18_eq, comparator_19_eq, comparator_20_eq, comparator_21_eq,
       comparator_22_eq, comparator_23_eq, comparator_24_eq, comparator_25_eq, comparator_26_eq,
       comparator_27_eq, comparator_28_eq, comparator_29_eq, comparator_30_eq, comparator_31_eq, WE_1, WE_2,
       WE_3, WE_4, WE_5, WE_6, WE_7, WE_8, WE_9, WE_10, WE_11, WE_12, WE_13, WE_14, WE_15, WE_16, WE_17,
       WE_18, WE_19, WE_20, WE_21, WE_22, WE_23, WE_24, WE_25, WE_26, WE_27, WE_28, WE_29, WE_30, WE_31;
  wire [31:0] x3, x4, x11, x12, x13, x14, x15, x16, x17, x18, x19, x20, x21, x22, x23, x24, x25, x26, x27,
       x28, x29, x30, x31;

  Comparator #(.width(5)) comparator_1 (.a(rd), .b(5'b00001), .eq(comparator_1_eq));  // open: gt, lt
  Comparator #(.width(5)) comparator_2 (.a(rd), .b(5'b00010), .eq(comparator_2_eq));  // open: gt, lt
  Comparator #(.width(5)) comparator_3 (.a(rd), .b(5'b00011), .eq(comparator_3_eq));  // open: gt, lt
  Comparator #(.width(5)) comparator_4 (.a(rd), .b(5'b00100), .eq(comparator_4_eq));  // open: gt, lt
  Comparator #(.width(5)) comparator_5 (.a(rd), .b(5'b00101), .eq(comparator_5_eq));  // open: gt, lt
  Comparator #(.width(5)) comparator_6 (.a(rd), .b(5'b00110), .eq(comparator_6_eq));  // open: gt, lt
  Comparator #(.width(5)) comparator_7 (.a(rd), .b(5'b00111), .eq(comparator_7_eq));  // open: gt, lt
  Comparator #(.width(5)) comparator_8 (.a(rd), .b(5'b01000), .eq(comparator_8_eq));  // open: gt, lt
  Comparator #(.width(5)) comparator_9 (.a(rd), .b(5'b01001), .eq(comparator_9_eq));  // open: gt, lt
  Comparator #(.width(5)) comparator_10 (.a(rd), .b(5'b01010), .eq(comparator_10_eq));  // open: gt, lt
  Comparator #(.width(5)) comparator_11 (.a(rd), .b(5'b01011), .eq(comparator_11_eq));  // open: gt, lt
  Comparator #(.width(5)) comparator_12 (.a(rd), .b(5'b01100), .eq(comparator_12_eq));  // open: gt, lt
  Comparator #(.width(5)) comparator_13 (.a(rd), .b(5'b01101), .eq(comparator_13_eq));  // open: gt, lt
  Comparator #(.width(5)) comparator_14 (.a(rd), .b(5'b01110), .eq(comparator_14_eq));  // open: gt, lt
  Comparator #(.width(5)) comparator_15 (.a(rd), .b(5'b01111), .eq(comparator_15_eq));  // open: gt, lt
  Comparator #(.width(5)) comparator_16 (.a(rd), .b(5'b10000), .eq(comparator_16_eq));  // open: gt, lt
  Comparator #(.width(5)) comparator_17 (.a(rd), .b(5'b10001), .eq(comparator_17_eq));  // open: gt, lt
  Comparator #(.width(5)) comparator_18 (.a(rd), .b(5'b10010), .eq(comparator_18_eq));  // open: gt, lt
  Comparator #(.width(5)) comparator_19 (.a(rd), .b(5'b10011), .eq(comparator_19_eq));  // open: gt, lt
  Comparator #(.width(5)) comparator_20 (.a(rd), .b(5'b10100), .eq(comparator_20_eq));  // open: gt, lt
  Comparator #(.width(5)) comparator_21 (.a(rd), .b(5'b10101), .eq(comparator_21_eq));  // open: gt, lt
  Comparator #(.width(5)) comparator_22 (.a(rd), .b(5'b10110), .eq(comparator_22_eq));  // open: gt, lt
  Comparator #(.width(5)) comparator_23 (.a(rd), .b(5'b10111), .eq(comparator_23_eq));  // open: gt, lt
  Comparator #(.width(5)) comparator_24 (.a(rd), .b(5'b11000), .eq(comparator_24_eq));  // open: gt, lt
  Comparator #(.width(5)) comparator_25 (.a(rd), .b(5'b11001), .eq(comparator_25_eq));  // open: gt, lt
  Comparator #(.width(5)) comparator_26 (.a(rd), .b(5'b11010), .eq(comparator_26_eq));  // open: gt, lt
  Comparator #(.width(5)) comparator_27 (.a(rd), .b(5'b11011), .eq(comparator_27_eq));  // open: gt, lt
  Comparator #(.width(5)) comparator_28 (.a(rd), .b(5'b11100), .eq(comparator_28_eq));  // open: gt, lt
  Comparator #(.width(5)) comparator_29 (.a(rd), .b(5'b11101), .eq(comparator_29_eq));  // open: gt, lt
  Comparator #(.width(5)) comparator_30 (.a(rd), .b(5'b11110), .eq(comparator_30_eq));  // open: gt, lt
  Comparator #(.width(5)) comparator_31 (.a(rd), .b({5{1'b1}}), .eq(comparator_31_eq));  // open: gt, lt
  and and_1 (WE_1, RegWEn, comparator_1_eq);
  and and_2 (WE_2, RegWEn, comparator_2_eq);
  and and_3 (WE_3, RegWEn, comparator_3_eq);
  and and_4 (WE_4, RegWEn, comparator_4_eq);
  and and_5 (WE_5, RegWEn, comparator_5_eq);
  and and_6 (WE_6, RegWEn, comparator_6_eq);
  and and_7 (WE_7, RegWEn, comparator_7_eq);
  and and_8 (WE_8, RegWEn, comparator_8_eq);
  and and_9 (WE_9, RegWEn, comparator_9_eq);
  and and_10 (WE_10, RegWEn, comparator_10_eq);
  and and_11 (WE_11, RegWEn, comparator_11_eq);
  and and_12 (WE_12, RegWEn, comparator_12_eq);
  and and_13 (WE_13, RegWEn, comparator_13_eq);
  and and_14 (WE_14, RegWEn, comparator_14_eq);
  and and_15 (WE_15, RegWEn, comparator_15_eq);
  and and_16 (WE_16, RegWEn, comparator_16_eq);
  and and_17 (WE_17, RegWEn, comparator_17_eq);
  and and_18 (WE_18, RegWEn, comparator_18_eq);
  and and_19 (WE_19, RegWEn, comparator_19_eq);
  and and_20 (WE_20, RegWEn, comparator_20_eq);
  and and_21 (WE_21, RegWEn, comparator_21_eq);
  and and_22 (WE_22, RegWEn, comparator_22_eq);
  and and_23 (WE_23, RegWEn, comparator_23_eq);
  and and_24 (WE_24, RegWEn, comparator_24_eq);
  and and_25 (WE_25, RegWEn, comparator_25_eq);
  and and_26 (WE_26, RegWEn, comparator_26_eq);
  and and_27 (WE_27, RegWEn, comparator_27_eq);
  and and_28 (WE_28, RegWEn, comparator_28_eq);
  and and_29 (WE_29, RegWEn, comparator_29_eq);
  and and_30 (WE_30, RegWEn, comparator_30_eq);
  and and_31 (WE_31, RegWEn, comparator_31_eq);
  Register #(.width(32)) x1 (.D(Write_Data), .en(WE_1), .clk(clk), .Q(ra));  // open: clr
  Register #(.width(32)) x2 (.D(Write_Data), .en(WE_2), .clk(clk), .Q(sp));  // open: clr
  Register #(.width(32)) register_1 (.D(Write_Data), .en(WE_3), .clk(clk), .Q(x3));  // open: clr
  Register #(.width(32)) register_2 (.D(Write_Data), .en(WE_4), .clk(clk), .Q(x4));  // open: clr
  Register #(.width(32)) register_3 (.D(Write_Data), .en(WE_5), .clk(clk), .Q(t0));  // open: clr
  Register #(.width(32)) register_4 (.D(Write_Data), .en(WE_6), .clk(clk), .Q(t1));  // open: clr
  Register #(.width(32)) register_5 (.D(Write_Data), .en(WE_7), .clk(clk), .Q(t2));  // open: clr
  Register #(.width(32)) register_6 (.D(Write_Data), .en(WE_8), .clk(clk), .Q(s0));  // open: clr
  Register #(.width(32)) register_7 (.D(Write_Data), .en(WE_9), .clk(clk), .Q(s1));  // open: clr
  Register #(.width(32)) register_8 (.D(Write_Data), .en(WE_10), .clk(clk), .Q(a0));  // open: clr
  Register #(.width(32)) register_9 (.D(Write_Data), .en(WE_11), .clk(clk), .Q(x11));  // open: clr
  Register #(.width(32)) register_10 (.D(Write_Data), .en(WE_12), .clk(clk), .Q(x12));  // open: clr
  Register #(.width(32)) register_11 (.D(Write_Data), .en(WE_13), .clk(clk), .Q(x13));  // open: clr
  Register #(.width(32)) register_12 (.D(Write_Data), .en(WE_14), .clk(clk), .Q(x14));  // open: clr
  Register #(.width(32)) register_13 (.D(Write_Data), .en(WE_15), .clk(clk), .Q(x15));  // open: clr
  Register #(.width(32)) register_14 (.D(Write_Data), .en(WE_16), .clk(clk), .Q(x16));  // open: clr
  Register #(.width(32)) register_15 (.D(Write_Data), .en(WE_17), .clk(clk), .Q(x17));  // open: clr
  Register #(.width(32)) register_16 (.D(Write_Data), .en(WE_18), .clk(clk), .Q(x18));  // open: clr
  Register #(.width(32)) register_17 (.D(Write_Data), .en(WE_19), .clk(clk), .Q(x19));  // open: clr
  Register #(.width(32)) register_18 (.D(Write_Data), .en(WE_20), .clk(clk), .Q(x20));  // open: clr
  Register #(.width(32)) register_19 (.D(Write_Data), .en(WE_21), .clk(clk), .Q(x21));  // open: clr
  Register #(.width(32)) register_20 (.D(Write_Data), .en(WE_22), .clk(clk), .Q(x22));  // open: clr
  Register #(.width(32)) register_21 (.D(Write_Data), .en(WE_23), .clk(clk), .Q(x23));  // open: clr
  Register #(.width(32)) register_22 (.D(Write_Data), .en(WE_24), .clk(clk), .Q(x24));  // open: clr
  Register #(.width(32)) register_23 (.D(Write_Data), .en(WE_25), .clk(clk), .Q(x25));  // open: clr
  Register #(.width(32)) register_24 (.D(Write_Data), .en(WE_26), .clk(clk), .Q(x26));  // open: clr
  Register #(.width(32)) register_25 (.D(Write_Data), .en(WE_27), .clk(clk), .Q(x27));  // open: clr
  Register #(.width(32)) register_26 (.D(Write_Data), .en(WE_28), .clk(clk), .Q(x28));  // open: clr
  Register #(.width(32)) register_27 (.D(Write_Data), .en(WE_29), .clk(clk), .Q(x29));  // open: clr
  Register #(.width(32)) register_28 (.D(Write_Data), .en(WE_30), .clk(clk), .Q(x30));  // open: clr
  Register #(.width(32)) register_29 (.D(Write_Data), .en(WE_31), .clk(clk), .Q(x31));  // open: clr
  Multiplexer #(.enable("false"), .select(5), .width(32)) multiplexer_1 (
    .in0({32{1'b0}}), .in1(ra), .in2(sp), .in3(x3), .in4(x4), .in5(t0), .in6(t1), .in7(t2), .in8(s0),
    .in9(s1), .in10(a0), .in11(x11), .in12(x12), .in13(x13), .in14(x14), .in15(x15), .in16(x16), .in17(x17),
    .in18(x18), .in19(x19), .in20(x20), .in21(x21), .in22(x22), .in23(x23), .in24(x24), .in25(x25),
    .in26(x26), .in27(x27), .in28(x28), .in29(x29), .in30(x30), .in31(x31), .out(Read_Data_1), .sel(rs1));
  Multiplexer #(.enable("false"), .select(5), .width(32)) multiplexer_2 (
    .in0({32{1'b0}}), .in1(ra), .in2(sp), .in3(x3), .in4(x4), .in5(t0), .in6(t1), .in7(t2), .in8(s0),
    .in9(s1), .in10(a0), .in11(x11), .in12(x12), .in13(x13), .in14(x14), .in15(x15), .in16(x16), .in17(x17),
    .in18(x18), .in19(x19), .in20(x20), .in21(x21), .in22(x22), .in23(x23), .in24(x24), .in25(x25),
    .in26(x26), .in27(x27), .in28(x28), .in29(x29), .in30(x30), .in31(x31), .out(Read_Data_2), .sel(rs2));

  // Other names for the same wires on the sheet: read_data1[31:0] = Read_Data_1; read_data2[31:0] = Read_Data_2;
  //   read_reg1[4:0] = rs1; read_reg2[4:0] = rs2; write_en = RegWEn; write_reg[4:0] = rd; x1[31:0] = ra;
  //   x2[31:0] = sp; x5[31:0] = t0; x6[31:0] = t1; x7[31:0] = t2; x8[31:0] = s0; x9[31:0] = s1; x10[31:0] = a0

  // Notes on the sheet:
  //   INPUTS to your circuit
  //   DON'T CHANGE THE LOCATIONS OF THE INPUTS AND OUTPUTS!
  //   These are DEBUG/TEST outputs from your circuit.
  //   OUTPUTS from your circuit
endmodule
